# Fritzing sketch Untitled Sketch (saved by Fritzing 0.9.3b)
breadboards: 4

parts:
  Part1 = Arduino Uno (Rev3)
  LED1 = smd LED [color="Red (633nm)" package="1206 [SMD]"]
  LED3 = smd LED [color="Yellow (595nm)" package="1206 [SMD]"]
  LED4 = smd LED [color="Green (560nm)" package="1206 [SMD]"]
  R1 = Resistor [tolerance=±5% resistance=220 package=THT]
  LED5 = smd LED [color="Red (633nm)" package="1206 [SMD]"]
  LED6 = smd LED [color="Green (560nm)" package="1206 [SMD]"]
  LED7 = smd LED [color="Green (560nm)" package="1206 [SMD]"]
  LED8 = smd LED [color="Red (633nm)" package="1206 [SMD]"]
  LED9 = smd LED [color="Red (633nm)" package="1206 [SMD]"]
  LED10 = smd LED [color="Yellow (595nm)" package="1206 [SMD]"]
  LED11 = smd LED [color="Yellow (595nm)" package="1206 [SMD]"]
  LED12 = smd LED [color="Green (560nm)" package="1206 [SMD]"]
  LED13 = smd LED [color="Yellow (595nm)" package="1206 [SMD]"]
  R2 = Resistor [tolerance=±5% resistance=220 package=THT]
  R3 = Resistor [tolerance=±5% resistance=220 package=THT]
  R4 = Resistor [tolerance=±5% resistance=220 package=THT]

nets:
  N1: Part1.A0, LED1.anode
  N2: Part1.A1, LED3.anode
  N3: Part1.A2, LED4.anode
  N4: Part1.D9_PWM, LED13.anode
  N5: Part1.D10_PWM/SS, LED7.anode
  N6: Part1.GND, R2.Pin_1, R4.Pin_1
  N7: Part1.D2, LED5.anode
  N8: Part1.D3_PWM, LED10.anode
  N9: Part1.D4, LED12.anode
  N10: Part1.D5_PWM, LED9.anode
  N11: Part1.D7, LED6.cathode
  N12: LED1.cathode, LED4.cathode, R1.Pin_0
  N13: LED5.cathode, LED10.cathode, LED12.cathode, R4.Pin_0
  N14: LED6.anode, LED9.cathode, LED11.cathode, R3.Pin_0
  N15: LED7.cathode, LED8.cathode, LED13.cathode, R2.Pin_0
